// Logisim project processor.circ as structural Verilog: 6 circuits, main circuit main
module main (
  input  [31:0] in_1,
  input  [31:0] in_2,
  output [31:0] out_3
);

  ALU alu_1 (.B(in_2), .A(in_1), .Y(out_3));  // open: F, out_4
endmodule

module ALU (
  input  [2:0] F,
  input  [31:0] B,
  input  [31:0] A,
  output out_4,
  output [31:0] Y
);

  wire bitselector_1_out, nor_1_out, nor_2_out, nor_3_out, nor_4_out, nor_5_out, nor_6_out, nor_7_out,
       nor_8_out;
  wire [31:0] adder_1_out, and_1_out, bit_extender_1_out, multiplexer_1_out, not_1_out, or_1_out;

  assign not_1_out = ~B;  // NOT_Gate not_1, 32 bits wide
  Multiplexer #(.width(32)) multiplexer_1 (.in0(B), .in1(not_1_out), .out(multiplexer_1_out), .sel(F[2]));
  Adder #(.width(32)) adder_1 (.a(multiplexer_1_out), .b(A), .out(adder_1_out), .cin(F[2]));  // open: cout
  BitSelector #(.width(32)) bitselector_1 (.in(adder_1_out), .out(bitselector_1_out), .sel(5'b10000));
  assign and_1_out = multiplexer_1_out & A;  // AND_Gate and_1, 32 bits wide
  assign or_1_out = multiplexer_1_out | A;  // OR_Gate or_1, 32 bits wide
  assign bit_extender_1_out = {{31{1'b0}}, bitselector_1_out};  // Bit_Extender bit_extender_1
  Multiplexer #(.select(2), .width(32)) multiplexer_2 (
    .in0(and_1_out), .in1(or_1_out), .in2(adder_1_out), .in3(bit_extender_1_out), .out(Y), .sel(F[1:0]));
  nor nor_1 (nor_1_out, Y[0], Y[1], Y[2], Y[3]);
  nor nor_2 (nor_2_out, Y[4], Y[5], Y[6], Y[7]);
  nor nor_3 (nor_3_out, Y[8], Y[9], Y[10], Y[11]);
  nor nor_4 (nor_4_out, Y[12], Y[13], Y[14], Y[15]);
  nor nor_5 (nor_5_out, Y[16], Y[17], Y[18], Y[19]);
  nor nor_6 (nor_6_out, Y[20], Y[21], Y[22], Y[23]);
  nor nor_7 (nor_7_out, Y[24], Y[25], Y[26], Y[27]);
  nor nor_8 (nor_8_out, Y[28], Y[29], Y[30], Y[31]);
  and and_2 (out_4, nor_1_out, nor_2_out, nor_3_out, nor_4_out, nor_5_out, nor_6_out, nor_7_out, nor_8_out);
endmodule

module Datapath (
  input  in_1,
  output [20:0] out_2,
  output [31:0] out_3,
  output [2:0] out_4,
  output [2:0] out_5,
  output [31:0] L_v0_3c7fd9f0,
  output [31:0] out_7,
  output [31:0] out_8,
  output [2:0] rd,
  output [31:0] out_10,
  output [4:0] out_11,
  output [4:0] out_12,
  output [4:0] out_13
);

  wire alu_1_out_4, and_1_out, clock_1_out, controlunit_1_alusrc, controlunit_1_branch, controlunit_1_regdst,
       controlunit_1_regwrite;
  wire [2:0] bitselector_7_out, controlunit_1_alucontrol;
  wire [7:0] adder_1_out, adder_2_out, bitselector_1_out, multiplexer_1_out, multiplexer_2_out, register_1_q,
       shifter_2_out;
  wire [10:0] bitselector_4_out;
  wire [15:0] bitselector_3_out, bitselector_8_out;
  wire [31:0] alu_1_y, rom_1_data, shifter_1_out;

  Multiplexer #(.disabled("Z"), .enable("true"), .width(8)) multiplexer_1 (
    .in0(adder_2_out), .in1(adder_1_out), .out(multiplexer_1_out), .sel(and_1_out));  // open: en
  Clock clock_1 (.out(clock_1_out));
  Multiplexer #(.disabled("Z"), .enable("true"), .width(8)) multiplexer_2 (
    .in0(multiplexer_1_out), .in1({8{1'b0}}), .out(multiplexer_2_out), .sel(in_1));  // open: en
  Register register_1 (.D(multiplexer_2_out), .Q(register_1_q), .clk(clock_1_out));  // open: en, clr
  Adder adder_1 (.a(adder_2_out), .b(bitselector_1_out), .out(adder_1_out));  // open: cin, cout
  Adder adder_2 (.a(register_1_q), .b(8'h4), .out(adder_2_out));  // open: cin, cout
  Shifter #(.width(32)) shifter_1 (.in(out_10), .\dist (5'b00010), .out(shifter_1_out));
  Shifter #(.shift("lr")) shifter_2 (.in(register_1_q), .\dist (3'b010), .out(shifter_2_out));
  BitSelector #(.group(8), .width(32)) bitselector_1 (.in(shifter_1_out), .out(bitselector_1_out), .sel(2'b00));
  ROM #(.dataWidth(32)) rom_1 (
    .addr(shifter_2_out), .data({rom_1_data[31:26], out_13, out_12, out_11, rom_1_data[10:0]}));
  BitSelector #(.group(21), .width(32)) bitselector_2 (
    .in({rom_1_data[31:26], out_13, out_12, out_11, rom_1_data[10:0]}), .out(out_2), .sel(1'b1));
  BitSelector #(.group(16), .width(32)) bitselector_3 (
    .in({rom_1_data[31:26], out_13, out_12, out_11, rom_1_data[10:0]}), .out(bitselector_3_out), .sel(1'b1));
  BitSelector #(.group(11), .width(32)) bitselector_4 (
    .in({rom_1_data[31:26], out_13, out_12, out_11, rom_1_data[10:0]}), .out(bitselector_4_out), .sel(2'b01));
  and and_1 (and_1_out, alu_1_out_4, controlunit_1_branch);
  ControlUnit controlunit_1 (
    .Instruction({rom_1_data[31:26], out_13, out_12, out_11, rom_1_data[10:0]}),
    .ALUSrc(controlunit_1_alusrc), .RegDst(controlunit_1_regdst), .RegWrite(controlunit_1_regwrite),
    .Branch(controlunit_1_branch), .ALUControl(controlunit_1_alucontrol));
  BitSelector #(.group(3), .width(21)) bitselector_5 (.in(out_2), .out(out_4), .sel(3'b000));
  BitSelector #(.group(3), .width(16)) bitselector_6 (.in(bitselector_3_out), .out(out_5), .sel(3'b000));
  BitSelector #(.group(3), .width(11)) bitselector_7 (.in(bitselector_4_out), .out(bitselector_7_out), .sel(2'b00));
  Multiplexer #(.disabled("Z"), .enable("true"), .width(3)) multiplexer_3 (
    .in0(out_5), .in1(bitselector_7_out), .out(rd), .sel(controlunit_1_regdst));  // open: en
  assign out_10 = {{16{bitselector_8_out[15]}}, bitselector_8_out};  // Bit_Extender bit_extender_1
  BitSelector #(.group(16), .width(32)) bitselector_8 (
    .in({rom_1_data[31:26], out_13, out_12, out_11, rom_1_data[10:0]}), .out(bitselector_8_out), .sel(1'b0));
  RegisterFile registerfile_1 (
    .WD3(alu_1_y), .A3(rd), .CLK(clock_1_out), .A2(out_5), .A1(out_4), .WE3(controlunit_1_regwrite),
    .RD1(out_3), .RD2(out_8), .V0(L_v0_3c7fd9f0));
  Multiplexer #(.disabled("Z"), .width(32)) multiplexer_4 (
    .in0(out_8), .in1(out_10), .out(out_7), .sel(controlunit_1_alusrc));
  ALU alu_1 (.B(out_7), .A(out_3), .F(controlunit_1_alucontrol), .out_4(alu_1_out_4), .Y(alu_1_y));

  // Other names for the same wires on the sheet: reset = in_1

  // Notes on the sheet:
  //   contents of rom_1 (hex, n*v repeats v):
  //   20040003 20030001 10040006 42820 33020 10000006 401820 2084ffff 1000fff9 601020 0 1000fffe 1020
  //   10a0fff8 461020 20a5ffff 1000fffc
  //   rs
  //   rt
  //   rt
  //   rs
  //   rd
endmodule

module Tests (
  output [31:0] Y,
  output [7:0] out_2,
  output [7:0] out_3,
  output [2:0] out_4
);

  BitSelector #(.group(8), .width(32)) bitselector_1 (.in(32'h12356789), .out(out_2), .sel(2'b01));
  BitSelector #(.group(8), .width(32)) bitselector_2 (.in(32'h12356789), .out(out_3), .sel(2'b01));
  BitSelector #(.group(3)) bitselector_3 (.in(out_3), .out(out_4), .sel(2'b00));

  assign Y = 32'hf4010207;

  // Notes on the sheet:
  //   binary values in Logisim. Convince yourself how the bits are displayed.
  //   Example 2: The bit selector is configured to have 32  
  //   bit group #1 (starting at index 0) is selected for the output.
  //   That is, the 8 bits 0x67 at bit indices 15..8  are sent to the output.
  //   Example 3: Now, assume that you want to extract 3 bits at   
  //   Example 1: A simple example that illustrates how 32-bit values are displayed as 
  //   input bits and 8 output bits. The parameter constant is 1, which means that   
  //   bit indices 10..8. This can be accoplished by putting two bit selecotrs in series.
endmodule

module RegisterFile (
  input  [2:0] A1,
  input  [31:0] WD3,
  input  CLK,
  input  [2:0] A2,
  input  WE3,
  input  [2:0] A3,
  output [31:0] RD1,
  output [31:0] RD2,
  output [31:0] V0
);

  wire and_1_out, and_2_out, and_3_out, and_4_out, and_5_out, and_6_out, and_7_out, decoder_1_out1,
       decoder_1_out2, decoder_1_out3, decoder_1_out4, decoder_1_out5, decoder_1_out6, decoder_1_out7;
  wire [31:0] register_1_q, register_3_q, register_4_q, register_5_q, register_6_q, register_7_q;

  Decoder #(.select(3)) decoder_1 (
    .out1(decoder_1_out1), .out2(decoder_1_out2), .out3(decoder_1_out3), .out4(decoder_1_out4),
    .out5(decoder_1_out5), .out6(decoder_1_out6), .out7(decoder_1_out7), .sel(A3));  // open: out0, en
  and and_1 (and_1_out, WE3, decoder_1_out1);
  and and_2 (and_2_out, WE3, decoder_1_out2);
  and and_3 (and_3_out, WE3, decoder_1_out3);
  and and_4 (and_4_out, WE3, decoder_1_out4);
  and and_5 (and_5_out, WE3, decoder_1_out5);
  and and_6 (and_6_out, WE3, decoder_1_out6);
  and and_7 (and_7_out, WE3, decoder_1_out7);
  Register #(.width(32)) register_1 (.D(WD3), .en(and_1_out), .clk(CLK), .Q(register_1_q), .clr(1'b0));
  Register #(.width(32)) register_2 (.D(WD3), .en(and_2_out), .clk(CLK), .Q(V0), .clr(1'b0));
  Register #(.width(32)) register_3 (.D(WD3), .en(and_3_out), .clk(CLK), .Q(register_3_q), .clr(1'b0));
  Register #(.width(32)) register_4 (.D(WD3), .en(and_4_out), .clk(CLK), .Q(register_4_q), .clr(1'b0));
  Register #(.width(32)) register_5 (.D(WD3), .en(and_5_out), .clk(CLK), .Q(register_5_q), .clr(1'b0));
  Register #(.width(32)) register_6 (.D(WD3), .en(and_6_out), .clk(CLK), .Q(register_6_q), .clr(1'b0));
  Register #(.width(32)) register_7 (.D(WD3), .en(and_7_out), .clk(CLK), .Q(register_7_q), .clr(1'b0));
  Multiplexer #(.enable("true"), .select(3), .width(32)) multiplexer_1 (
    .in0({32{1'b0}}), .in1(register_1_q), .in2(V0), .in3(register_3_q), .in4(register_4_q),
    .in5(register_5_q), .in6(register_6_q), .in7(register_7_q), .out(RD1), .sel(A1));  // open: en
  Multiplexer #(.enable("true"), .select(3), .width(32)) multiplexer_2 (
    .in0({32{1'b0}}), .in1(register_1_q), .in2(V0), .in3(register_3_q), .in4(register_4_q),
    .in5(register_5_q), .in6(register_6_q), .in7(register_7_q), .out(RD2), .sel(A2));  // open: en
endmodule

module ControlUnit (
  input  [31:0] Instruction,
  output RegDst,
  output RegWrite,
  output ALUSrc,
  output [2:0] ALUControl,
  output Branch
);

  wire and_2_out, not_1_out, not_2_out, not_3_out, or_1_out;
  wire [5:0] bitselector_1_out;
  wire [31:0] shifter_1_out;

  Shifter #(.shift("lr"), .width(32)) shifter_1 (.in(Instruction), .\dist (5'b11010), .out(shifter_1_out));
  BitSelector #(.group(6), .width(32)) bitselector_1 (.in(shifter_1_out), .out(bitselector_1_out), .sel(3'b000));
  Comparator #(.mode("unsigned"), .width(6)) comparator_1 (
    .a(bitselector_1_out), .b(6'b001000), .eq(ALUSrc));  // open: gt, lt
  Comparator #(.mode("unsigned"), .width(6)) comparator_2 (
    .a(bitselector_1_out), .b({6{1'b0}}), .eq(RegDst));  // open: gt, lt
  Comparator #(.mode("unsigned"), .width(6)) comparator_3 (
    .a(bitselector_1_out), .b(6'b000100), .eq(Branch));  // open: gt, lt
  or or_1 (or_1_out, ALUSrc, RegDst);
  not not_1 (not_1_out, Branch);
  and and_1 (RegWrite, or_1_out, not_1_out);
  not not_2 (not_2_out, ALUSrc);
  not not_3 (not_3_out, RegDst);
  and and_2 (and_2_out, not_2_out, not_3_out, Branch);
  Multiplexer #(.width(3)) multiplexer_1 (.in0(3'b010), .in1(3'b110), .out(ALUControl), .sel(and_2_out));

  // Notes on the sheet:
  //   get the op code
  //   get only the 6lsb
  //   check if ==8
  //   this is addi
  //   check if ==0
  //   this is add
  //   if opcode==4
  //   this is beq
  //   first bit of alu
endmodule
